// Logisim project CPU.circ as structural Verilog: 35 circuits, main circuit CPU
// ALU
module ALU_update (
  input  [1:0] control,
  input  [31:0] A,
  input  [31:0] B,
  output [31:0] out,
  output z,
  output n,
  output carry,
  output overflow
);

  wire [31:0] n32_bit_adder_1_out, n32_bit_and_1_out_3, n32_bit_or_1_out_3;

  _32_bit_AND u_32_bit_and_1 (.A(A), .B(B), .out_3(n32_bit_and_1_out_3));
  _32_bit_or u_32_bit_or_1 (.A(A), .B(B), .out_3(n32_bit_or_1_out_3));
  _32_bit_adder u_32_bit_adder_1 (
    .in_1(control[0]), .A(A), .B(B), .out(n32_bit_adder_1_out), .cout(carry), .overfflow(overflow));
  Multiplexer #(.select(2), .width(32), .enable("false")) multiplexer_1 (
    .in0(n32_bit_and_1_out_3), .in1(n32_bit_or_1_out_3), .in2(n32_bit_adder_1_out),
    .in3(n32_bit_adder_1_out), .out(out), .sel(control));
  zero_flag zero_flag_1 (.in(out), .out(z));
  neg_flag neg_flag_1 (.in_1(out), .out(n));

  // Notes on the sheet:
  //   2207109
  //   0 0 - AND
  //   0 1 - OR
  //   1 0 - ADDER
  //   1 1 - Subtractor
endmodule

module CLG (
  input  [3:0] A,
  input  [3:0] B,
  input  CIN,
  output [3:0] O
);

  wire and_1_out, and_2_out, and_3_out, and_4_out, and_5_out, and_6_out, and_7_out, and_8_out, and_9_out,
       and_10_out, G0_out, G1_out, G2_out, G3_out, P0_out, P1_out, P2_out, P3_out;

  and G3 (G3_out, B[3], A[3]);
  and and_1 (and_1_out, G2_out, P3_out);
  and and_2 (and_2_out, G1_out, P2_out, P3_out);
  or or_1 (O[3], G3_out, and_1_out, and_4_out, and_2_out, and_3_out);
  xor P3 (P3_out, B[3], A[3]);
  and and_3 (and_3_out, G0_out, P1_out, P2_out, P3_out);
  and and_4 (and_4_out, P3_out, P2_out, P1_out, P0_out, CIN);
  and G2 (G2_out, B[2], A[2]);
  and and_5 (and_5_out, G1_out, P2_out);
  xor P2 (P2_out, B[2], A[2]);
  and and_6 (and_6_out, P2_out, P1_out, G0_out);
  and and_7 (and_7_out, P2_out, P1_out, P0_out, CIN);
  or or_2 (O[2], G2_out, and_5_out, and_6_out, and_7_out);
  and G1 (G1_out, B[1], A[1]);
  and and_8 (and_8_out, G0_out, P1_out);
  xor P1 (P1_out, B[1], A[1]);
  and and_9 (and_9_out, CIN, P0_out, P1_out);
  or or_3 (O[1], G1_out, and_8_out, and_9_out);
  and G0 (G0_out, B[0], A[0]);
  or or_4 (O[0], G0_out, and_10_out);
  xor P0 (P0_out, B[0], A[0]);
  and and_10 (and_10_out, CIN, P0_out);

  // Notes on the sheet:
  //   2207109
endmodule

module _4_bit_adder (
  input  [3:0] carry_in,
  input  [3:0] A,
  input  [3:0] B,
  output [3:0] out_4
);

  _1_BIT_ADDER u_1_bit_adder_1 (.cin(carry_in[0]), .b(B[0]), .a(A[0]), .sum(out_4[0]));  // open: carry
  _1_BIT_ADDER u_1_bit_adder_2 (.cin(carry_in[1]), .b(B[1]), .a(A[1]), .sum(out_4[1]));  // open: carry
  _1_BIT_ADDER u_1_bit_adder_3 (.cin(carry_in[2]), .b(B[2]), .a(A[2]), .sum(out_4[2]));  // open: carry
  _1_BIT_ADDER u_1_bit_adder_4 (.cin(carry_in[3]), .b(B[3]), .a(A[3]), .sum(out_4[3]));  // open: carry
endmodule

// adder
module _1_BIT_ADDER (
  input  cin,
  input  b,
  input  a,
  output sum,
  output carry
);

  wire and_1_out, and_2_out, xor_1_out;

  and and_1 (and_1_out, cin, xor_1_out);
  or or_1 (carry, and_1_out, and_2_out);
  and and_2 (and_2_out, b, a);
  xor xor_1 (xor_1_out, b, a);
  xor xor_2 (sum, cin, xor_1_out);
endmodule

// Adder
module _32_bit_adder (
  input  in_1,
  input  [31:0] A,
  input  [31:0] B,
  output [31:0] out,
  output cout,
  output overfflow
);

  wire and_1_out, and_2_out, not_1_out, not_2_out, not_3_out;
  wire [30:0] n32_bit_clg_1_out_4;
  wire [31:0] bit_extender_1_out, xor_1_out;

  assign bit_extender_1_out = {{31{in_1}}, in_1};  // Bit_Extender bit_extender_1
  assign xor_1_out = B ^ bit_extender_1_out;  // XOR_Gate xor_1, 32 bits wide
  _32_bit_clg u_32_bit_clg_1 (.cin(in_1), .A(A), .B(xor_1_out), .out_4({cout, n32_bit_clg_1_out_4}));
  _4_bit_adder u_4_bit_adder_1 (
    .carry_in({n32_bit_clg_1_out_4[2:0], in_1}), .A(A[3:0]), .B(xor_1_out[3:0]), .out_4(out[3:0]));
  _4_bit_adder u_4_bit_adder_2 (.carry_in(n32_bit_clg_1_out_4[6:3]), .A(A[7:4]), .B(xor_1_out[7:4]), .out_4(out[7:4]));
  _4_bit_adder u_4_bit_adder_3 (
    .carry_in(n32_bit_clg_1_out_4[10:7]), .A(A[11:8]), .B(xor_1_out[11:8]), .out_4(out[11:8]));
  _4_bit_adder u_4_bit_adder_4 (
    .carry_in(n32_bit_clg_1_out_4[14:11]), .A(A[15:12]), .B(xor_1_out[15:12]), .out_4(out[15:12]));
  _4_bit_adder u_4_bit_adder_5 (
    .carry_in(n32_bit_clg_1_out_4[18:15]), .A(A[19:16]), .B(xor_1_out[19:16]), .out_4(out[19:16]));
  _4_bit_adder u_4_bit_adder_6 (
    .carry_in(n32_bit_clg_1_out_4[22:19]), .A(A[23:20]), .B(xor_1_out[23:20]), .out_4(out[23:20]));
  _4_bit_adder u_4_bit_adder_7 (
    .carry_in(n32_bit_clg_1_out_4[26:23]), .A(A[27:24]), .B(xor_1_out[27:24]), .out_4(out[27:24]));
  _4_bit_adder u_4_bit_adder_8 (
    .carry_in(n32_bit_clg_1_out_4[30:27]), .A(A[31:28]), .B(xor_1_out[31:28]), .out_4(out[31:28]));
  not not_1 (not_1_out, A[31]);
  not not_2 (not_2_out, xor_1_out[31]);
  and and_1 (and_1_out, not_1_out, not_2_out, out[31]);
  not not_3 (not_3_out, out[31]);
  or or_1 (overfflow, and_1_out, and_2_out);
  and and_2 (and_2_out, not_3_out, A[31], xor_1_out[31]);
endmodule

module _32_bit_clg (
  input  cin,
  input  [31:0] A,
  input  [31:0] B,
  output [31:0] out_4
);

  CLG clg_1 (.A(A[3:0]), .B(B[3:0]), .O(out_4[3:0]), .CIN(cin));
  CLG clg_2 (.A(A[7:4]), .B(B[7:4]), .O(out_4[7:4]), .CIN(out_4[3]));
  CLG clg_3 (.A(A[11:8]), .B(B[11:8]), .O(out_4[11:8]), .CIN(out_4[7]));
  CLG clg_4 (.A(A[15:12]), .B(B[15:12]), .O(out_4[15:12]), .CIN(out_4[11]));
  CLG clg_5 (.A(A[19:16]), .B(B[19:16]), .O(out_4[19:16]), .CIN(out_4[15]));
  CLG clg_6 (.A(A[23:20]), .B(B[23:20]), .O(out_4[23:20]), .CIN(out_4[19]));
  CLG clg_7 (.A(A[27:24]), .B(B[27:24]), .O(out_4[27:24]), .CIN(out_4[23]));
  CLG clg_8 (.A(A[31:28]), .B(B[31:28]), .O(out_4[31:28]), .CIN(out_4[27]));
endmodule

// AND
module _32_bit_AND (
  input  [31:0] A,
  input  [31:0] B,
  output [31:0] out_3
);

  assign out_3 = A & B;  // AND_Gate and_1, 32 bits wide
endmodule

// OR
module _32_bit_or (
  input  [31:0] A,
  input  [31:0] B,
  output [31:0] out_3
);

  assign out_3 = A | B;  // OR_Gate or_1, 32 bits wide
endmodule

// zero
module zero_flag (
  input  [31:0] in,
  output out
);

  wire or_1_out;

  or or_1 (or_1_out, in[0], in[1], in[2], in[3], in[4], in[5], in[6], in[7], in[8], in[9], in[10], in[11], in[12], in[13], in[14], in[15], in[16], in[17], in[18], in[19], in[20], in[21], in[22], in[23], in[24], in[25], in[26], in[27], in[28], in[29], in[30], in[31]);
  not not_1 (out, or_1_out);
endmodule

// neg
module neg_flag (
  input  [31:0] in_1,
  output out
);


  assign out = in_1[31];
endmodule

module ALU (
  input  [1:0] control,
  input  [31:0] A,
  input  [31:0] B,
  output [31:0] result,
  output z,
  output n,
  output carry,
  output overflow
);

  wire [31:0] n32_bit_adder_1_out, n32_bit_and_1_out_3, n32_bit_or_1_out_3;

  _32_bit_AND u_32_bit_and_1 (.A(A), .B(B), .out_3(n32_bit_and_1_out_3));
  _32_bit_or u_32_bit_or_1 (.A(A), .B(B), .out_3(n32_bit_or_1_out_3));
  _32_bit_adder u_32_bit_adder_1 (
    .in_1(control[0]), .A(A), .B(B), .out(n32_bit_adder_1_out), .cout(carry), .overfflow(overflow));
  Multiplexer #(.select(2), .width(32)) multiplexer_1 (
    .in0(n32_bit_adder_1_out), .in1(n32_bit_adder_1_out), .in2(n32_bit_and_1_out_3),
    .in3(n32_bit_or_1_out_3), .out(result), .sel(control));  // open: en
  zero_flag zero_flag_1 (.in(result), .out(z));
  neg_flag neg_flag_1 (.in_1(result), .out(n));

  // Notes on the sheet:
  //   2207109
  //   0 0 - Adder
  //   0 1 - Subtractor
  //   1 0 - AND
  //   1 1 - OR
endmodule

module multiplier (
  input  [31:0] M,
  input  [31:0] Q,
  input  in_3,
  output [31:0] out_4,
  output [31:0] out_5
);

  wire clock_1_out, controller_1_dec, controller_1_load, controller_1_load_a, controller_1_set,
       controller_1_shift_reg, or_1_out, Q_1_out, Q_out, shift_register_1_out;
  wire [1:0] controller_1_c0;
  wire [5:0] counter_1_q;
  wire [31:0] alu_update_1_out, complement_1_out_2, complement_2_out_2, shift_register_2_q31;

  Clock clock_1 (.out(clock_1_out));
  controller controller_1 (
    .clk(clock_1_out), .Q0(out_5[0]), .Q_1(Q_1_out), .reset(in_3), .counter(counter_1_q),
    .Set(controller_1_set), .load(controller_1_load), .Load_A(controller_1_load_a), .C0(controller_1_c0[0]),
    .C1(controller_1_c0[1]), .Shift_reg(controller_1_shift_reg), .Dec(controller_1_dec));
  complement complement_1 (.in_1(M), .out_2(complement_1_out_2));
  complement complement_2 (.in_1(Q), .out_2(complement_2_out_2));
  or or_1 (or_1_out, controller_1_load, controller_1_dec);
  Shift_Register #(.length(32)) shift_register_1 (
    .shift(controller_1_shift_reg), .in(out_4[31]), .clk(clock_1_out), .out(shift_register_1_out),
    .load(controller_1_load_a), .clr(controller_1_set), .d0(alu_update_1_out[31]), .q0(out_4[31]),
    .d1(alu_update_1_out[30]), .q1(out_4[30]), .d2(alu_update_1_out[29]), .q2(out_4[29]),
    .d3(alu_update_1_out[28]), .q3(out_4[28]), .d4(alu_update_1_out[27]), .q4(out_4[27]),
    .d5(alu_update_1_out[26]), .q5(out_4[26]), .d6(alu_update_1_out[25]), .q6(out_4[25]),
    .d7(alu_update_1_out[24]), .q7(out_4[24]), .d8(alu_update_1_out[23]), .q8(out_4[23]),
    .d9(alu_update_1_out[22]), .q9(out_4[22]), .d10(alu_update_1_out[21]), .q10(out_4[21]),
    .d11(alu_update_1_out[20]), .q11(out_4[20]), .d12(alu_update_1_out[19]), .q12(out_4[19]),
    .d13(alu_update_1_out[18]), .q13(out_4[18]), .d14(alu_update_1_out[17]), .q14(out_4[17]),
    .d15(alu_update_1_out[16]), .q15(out_4[16]), .d16(alu_update_1_out[15]), .q16(out_4[15]),
    .d17(alu_update_1_out[14]), .q17(out_4[14]), .d18(alu_update_1_out[13]), .q18(out_4[13]),
    .d19(alu_update_1_out[12]), .q19(out_4[12]), .d20(alu_update_1_out[11]), .q20(out_4[11]),
    .d21(alu_update_1_out[10]), .q21(out_4[10]), .d22(alu_update_1_out[9]), .q22(out_4[9]),
    .d23(alu_update_1_out[8]), .q23(out_4[8]), .d24(alu_update_1_out[7]), .q24(out_4[7]),
    .d25(alu_update_1_out[6]), .q25(out_4[6]), .d26(alu_update_1_out[5]), .q26(out_4[5]),
    .d27(alu_update_1_out[4]), .q27(out_4[4]), .d28(alu_update_1_out[3]), .q28(out_4[3]),
    .d29(alu_update_1_out[2]), .q29(out_4[2]), .d30(alu_update_1_out[1]), .q30(out_4[1]),
    .d31(alu_update_1_out[0]), .q31(out_4[0]));
  Counter #(.width(6), .max('h3f)) counter_1 (
    .load(or_1_out), .D(6'b100000), .count(controller_1_dec), .Q(counter_1_q), .clk(clock_1_out));  // open: carry, clr
  Shift_Register #(.length(32)) shift_register_2 (
    .shift(1'b0), .clk(clock_1_out), .load(controller_1_load), .d0(complement_1_out_2[31]),
    .q0(shift_register_2_q31[31]), .d1(complement_1_out_2[30]), .q1(shift_register_2_q31[30]),
    .d2(complement_1_out_2[29]), .q2(shift_register_2_q31[29]), .d3(complement_1_out_2[28]),
    .q3(shift_register_2_q31[28]), .d4(complement_1_out_2[27]), .q4(shift_register_2_q31[27]),
    .d5(complement_1_out_2[26]), .q5(shift_register_2_q31[26]), .d6(complement_1_out_2[25]),
    .q6(shift_register_2_q31[25]), .d7(complement_1_out_2[24]), .q7(shift_register_2_q31[24]),
    .d8(complement_1_out_2[23]), .q8(shift_register_2_q31[23]), .d9(complement_1_out_2[22]),
    .q9(shift_register_2_q31[22]), .d10(complement_1_out_2[21]), .q10(shift_register_2_q31[21]),
    .d11(complement_1_out_2[20]), .q11(shift_register_2_q31[20]), .d12(complement_1_out_2[19]),
    .q12(shift_register_2_q31[19]), .d13(complement_1_out_2[18]), .q13(shift_register_2_q31[18]),
    .d14(complement_1_out_2[17]), .q14(shift_register_2_q31[17]), .d15(complement_1_out_2[16]),
    .q15(shift_register_2_q31[16]), .d16(complement_1_out_2[15]), .q16(shift_register_2_q31[15]),
    .d17(complement_1_out_2[14]), .q17(shift_register_2_q31[14]), .d18(complement_1_out_2[13]),
    .q18(shift_register_2_q31[13]), .d19(complement_1_out_2[12]), .q19(shift_register_2_q31[12]),
    .d20(complement_1_out_2[11]), .q20(shift_register_2_q31[11]), .d21(complement_1_out_2[10]),
    .q21(shift_register_2_q31[10]), .d22(complement_1_out_2[9]), .q22(shift_register_2_q31[9]),
    .d23(complement_1_out_2[8]), .q23(shift_register_2_q31[8]), .d24(complement_1_out_2[7]),
    .q24(shift_register_2_q31[7]), .d25(complement_1_out_2[6]), .q25(shift_register_2_q31[6]),
    .d26(complement_1_out_2[5]), .q26(shift_register_2_q31[5]), .d27(complement_1_out_2[4]),
    .q27(shift_register_2_q31[4]), .d28(complement_1_out_2[3]), .q28(shift_register_2_q31[3]),
    .d29(complement_1_out_2[2]), .q29(shift_register_2_q31[2]), .d30(complement_1_out_2[1]),
    .q30(shift_register_2_q31[1]), .d31(complement_1_out_2[0]), .q31(shift_register_2_q31[0]));  // open: in, out, clr
  ALU_update alu_update_1 (
    .control(controller_1_c0), .A(out_4), .B(shift_register_2_q31), .out(alu_update_1_out));  // open: z, n, carry, overflow
  Shift_Register #(.length(32)) u_Q (
    .shift(controller_1_shift_reg), .in(shift_register_1_out), .clk(clock_1_out), .out(Q_out),
    .load(controller_1_load), .d0(complement_2_out_2[31]), .q0(out_5[31]), .d1(complement_2_out_2[30]),
    .q1(out_5[30]), .d2(complement_2_out_2[29]), .q2(out_5[29]), .d3(complement_2_out_2[28]), .q3(out_5[28]),
    .d4(complement_2_out_2[27]), .q4(out_5[27]), .d5(complement_2_out_2[26]), .q5(out_5[26]),
    .d6(complement_2_out_2[25]), .q6(out_5[25]), .d7(complement_2_out_2[24]), .q7(out_5[24]),
    .d8(complement_2_out_2[23]), .q8(out_5[23]), .d9(complement_2_out_2[22]), .q9(out_5[22]),
    .d10(complement_2_out_2[21]), .q10(out_5[21]), .d11(complement_2_out_2[20]), .q11(out_5[20]),
    .d12(complement_2_out_2[19]), .q12(out_5[19]), .d13(complement_2_out_2[18]), .q13(out_5[18]),
    .d14(complement_2_out_2[17]), .q14(out_5[17]), .d15(complement_2_out_2[16]), .q15(out_5[16]),
    .d16(complement_2_out_2[15]), .q16(out_5[15]), .d17(complement_2_out_2[14]), .q17(out_5[14]),
    .d18(complement_2_out_2[13]), .q18(out_5[13]), .d19(complement_2_out_2[12]), .q19(out_5[12]),
    .d20(complement_2_out_2[11]), .q20(out_5[11]), .d21(complement_2_out_2[10]), .q21(out_5[10]),
    .d22(complement_2_out_2[9]), .q22(out_5[9]), .d23(complement_2_out_2[8]), .q23(out_5[8]),
    .d24(complement_2_out_2[7]), .q24(out_5[7]), .d25(complement_2_out_2[6]), .q25(out_5[6]),
    .d26(complement_2_out_2[5]), .q26(out_5[5]), .d27(complement_2_out_2[4]), .q27(out_5[4]),
    .d28(complement_2_out_2[3]), .q28(out_5[3]), .d29(complement_2_out_2[2]), .q29(out_5[2]),
    .d30(complement_2_out_2[1]), .q30(out_5[1]), .d31(complement_2_out_2[0]), .q31(out_5[0]));  // open: clr
  Shift_Register #(.length(1)) Q_1 (
    .shift(controller_1_shift_reg), .in(Q_out), .clk(clock_1_out), .out(Q_1_out), .clr(controller_1_set));  // open: load, d0, q0

  // Notes on the sheet:
  //   2207109
endmodule

module complement (
  input  [31:0] in_1,
  output [31:0] out_2
);

  wire [30:0] not_1_out;
  wire [31:0] alu_update_1_out;

  not not_1 (not_1_out[0], in_1[0]);
  not not_2 (not_1_out[1], in_1[1]);
  not not_3 (not_1_out[2], in_1[2]);
  not not_4 (not_1_out[3], in_1[3]);
  not not_5 (not_1_out[4], in_1[4]);
  not not_6 (not_1_out[5], in_1[5]);
  not not_7 (not_1_out[6], in_1[6]);
  not not_8 (not_1_out[7], in_1[7]);
  not not_9 (not_1_out[8], in_1[8]);
  not not_10 (not_1_out[9], in_1[9]);
  not not_11 (not_1_out[10], in_1[10]);
  not not_12 (not_1_out[11], in_1[11]);
  not not_13 (not_1_out[12], in_1[12]);
  not not_14 (not_1_out[13], in_1[13]);
  not not_15 (not_1_out[14], in_1[14]);
  not not_16 (not_1_out[15], in_1[15]);
  not not_17 (not_1_out[16], in_1[16]);
  not not_18 (not_1_out[17], in_1[17]);
  not not_19 (not_1_out[18], in_1[18]);
  not not_20 (not_1_out[19], in_1[19]);
  not not_21 (not_1_out[20], in_1[20]);
  not not_22 (not_1_out[21], in_1[21]);
  not not_23 (not_1_out[22], in_1[22]);
  not not_24 (not_1_out[23], in_1[23]);
  not not_25 (not_1_out[24], in_1[24]);
  not not_26 (not_1_out[25], in_1[25]);
  not not_27 (not_1_out[26], in_1[26]);
  not not_28 (not_1_out[27], in_1[27]);
  not not_29 (not_1_out[28], in_1[28]);
  not not_30 (not_1_out[29], in_1[29]);
  not not_31 (not_1_out[30], in_1[30]);
  Multiplexer #(.width(32), .enable("false")) multiplexer_1 (
    .in0(in_1), .in1(alu_update_1_out), .out(out_2), .sel(in_1[31]));
  ALU_update alu_update_1 (
    .control(2'b10), .A(32'h1), .B({in_1[31], not_1_out}), .out(alu_update_1_out));  // open: z, n, carry, overflow
endmodule

module counter (
  input  [2:0] T,
  input  C,
  input  [1:0] Q,
  output DA,
  output DB,
  output DC
);

  wire and_1_out, and_2_out, and_3_out, and_4_out, and_5_out, or_3_out, or_5_out, Q0, Q1, Q2, Q3, T0, T1, T2,
       T3, T4, T5, T6, T7;

  Decoder #(.select(3), .enable("false")) decoder_1 (
    .out0(T0), .out1(T1), .out2(T2), .out3(T3), .out4(T4), .out5(T5), .out6(T6), .out7(T7), .sel(T));
  or or_1 (DA, T0, and_3_out, T3, T4, and_2_out, T7);
  or or_2 (DB, T1, and_1_out, T5, T6, T6, T7);
  and and_1 (and_1_out, T2, Q2);
  and and_2 (and_2_out, T6, C);
  and and_3 (and_3_out, T2, or_3_out);
  or or_3 (or_3_out, Q0, Q2, Q3);
  or or_4 (DC, T5, and_4_out, T3, T4, and_5_out, T7);
  Decoder #(.select(2), .enable("false")) decoder_2 (.out0(Q0), .out1(Q1), .out2(Q2), .out3(Q3), .sel(Q));
  and and_4 (and_4_out, T2, or_5_out);
  or or_5 (or_5_out, Q0, Q1, Q3);
  and and_5 (and_5_out, T6, C);
endmodule

module controller (
  input  clk,
  input  Q0,
  input  Q_1,
  input  reset,
  input  [5:0] counter,
  output Set,
  output load,
  output Load_A,
  output C0,
  output C1,
  output Shift_reg,
  output Dec
);

  wire counter_1_da, counter_1_db, counter_1_dc, nor_1_out, T0, T2, T4, T6, T7;
  wire [2:0] T;

  nor nor_1 (nor_1_out, counter[0], counter[1], counter[2], counter[3], counter[4], counter[5]);
  or or_1 (Load_A, C0, T4);
  or or_2 (C1, T4, C0);
  counter counter_1 (.Q({Q0, Q_1}), .T(T), .C(nor_1_out), .DA(counter_1_da), .DB(counter_1_db), .DC(counter_1_dc));
  Decoder #(.select(3), .enable("false")) decoder_1 (
    .out0(T0), .out1(load), .out2(T2), .out3(C0), .out4(T4), .out5(Dec), .out6(T6), .out7(T7), .sel(T));
  D_Flip_Flop d_ff_1 (.clk(clk), .D(counter_1_da), .Q(T[0]), .reset(reset));  // open: Qn, preset, en
  D_Flip_Flop d_ff_2 (.clk(clk), .D(counter_1_db), .Q(T[1]), .reset(reset));  // open: Qn, preset, en
  D_Flip_Flop d_ff_3 (.clk(clk), .D(counter_1_dc), .Q(T[2]), .reset(reset));  // open: Qn, preset, en

  assign Set = load;
  assign Shift_reg = Dec;

  // Other names for the same wires on the sheet: T1 = load; T3 = C0; T5 = Dec
endmodule

// 4 bit load reg
module Load_register (
  input  reset,
  input  Clock,
  input  load,
  input  [3:0] Input,
  output [3:0] \output 
);

  wire and_1_out, and_2_out, and_3_out, and_4_out, and_5_out, and_6_out, and_7_out, and_8_out, not_1_out,
       not_2_out, not_3_out, not_4_out, or_1_out, or_2_out, or_3_out, or_4_out;

  not not_1 (not_1_out, load);
  not not_2 (not_2_out, load);
  not not_3 (not_3_out, load);
  not not_4 (not_4_out, load);
  Clock clock_1 ();  // open: out
  and and_1 (and_1_out, \output [0], not_1_out);
  and and_2 (and_2_out, Input[0], load);
  and and_3 (and_3_out, \output [1], not_2_out);
  and and_4 (and_4_out, Input[1], load);
  and and_5 (and_5_out, \output [2], not_3_out);
  and and_6 (and_6_out, Input[2], load);
  and and_7 (and_7_out, \output [3], not_4_out);
  and and_8 (and_8_out, Input[3], load);
  or or_1 (or_1_out, and_1_out, and_2_out);
  or or_2 (or_2_out, and_3_out, and_4_out);
  or or_3 (or_3_out, and_5_out, and_6_out);
  or or_4 (or_4_out, and_7_out, and_8_out);
  D_Flip_Flop d_ff_1 (.clk(Clock), .D(or_1_out), .Q(\output [0]), .reset(reset));  // open: Qn, preset, en
  D_Flip_Flop d_ff_2 (.clk(Clock), .D(or_2_out), .Q(\output [1]), .reset(reset));  // open: Qn, preset, en
  D_Flip_Flop d_ff_3 (.clk(Clock), .D(or_3_out), .Q(\output [2]), .reset(reset));  // open: Qn, preset, en
  D_Flip_Flop d_ff_4 (.clk(Clock), .D(or_4_out), .Q(\output [3]), .reset(reset));  // open: Qn, preset, en

  // Notes on the sheet:
  //   2207109
endmodule

module _8_bit_Load_reg (
  input  Clock,
  input  reset,
  input  load,
  input  [7:0] in,
  output [7:0] out
);

  Load_register load_register_1 (.Input(in[3:0]), .\output (out[3:0]), .load(load), .Clock(Clock), .reset(reset));
  Load_register load_register_2 (.Input(in[7:4]), .\output (out[7:4]), .load(load), .Clock(Clock), .reset(reset));

  // Notes on the sheet:
  //   2207109
endmodule

module _16_bit_load_reg (
  input  Clock,
  input  reset,
  input  load,
  input  [15:0] in,
  output [15:0] out
);

  _8_bit_Load_reg u_8_bit_load_reg_1 (.load(load), .in(in[7:0]), .out(out[7:0]), .Clock(Clock), .reset(reset));
  _8_bit_Load_reg u_8_bit_load_reg_2 (.load(load), .in(in[15:8]), .out(out[15:8]), .Clock(Clock), .reset(reset));

  // Notes on the sheet:
  //   2207109
endmodule

module _32_bit_load_reg (
  input  Clock,
  input  reset,
  input  load,
  input  [31:0] in,
  output [31:0] out
);

  _16_bit_load_reg u_16_bit_load_reg_1 (.load(load), .in(in[15:0]), .out(out[15:0]), .Clock(Clock), .reset(reset));
  _16_bit_load_reg u_16_bit_load_reg_2 (.load(load), .in(in[31:16]), .out(out[31:16]), .Clock(Clock), .reset(reset));

  // Notes on the sheet:
  //   2207109
endmodule

// Acc
module Accumulator (
  input  reset,
  input  load,
  input  Clock,
  input  [31:0] in,
  output [31:0] out
);

  _32_bit_load_reg u_32_bit_load_reg_1 (.load(load), .in(in), .out(out), .Clock(Clock), .reset(reset));

  // Notes on the sheet:
  //   2207109
endmodule

module MBR (
  input  load,
  input  count,
  input  clock,
  input  reset,
  input  [31:0] in,
  output [31:0] out,
  output MBR_zero
);

  wire n4_bit_counter_1_cout, n4_bit_counter_2_cout, n4_bit_counter_3_cout, n4_bit_counter_4_cout,
       n4_bit_counter_5_cout, n4_bit_counter_6_cout, n4_bit_counter_7_cout, or_1_out;

  _4_bit_counter u_4_bit_counter_1 (
    .reset(reset), .count(count), .load(load), .\input (in[3:0]), .out(out[3:0]),
    .cout(n4_bit_counter_1_cout), .clock(clock));
  _4_bit_counter u_4_bit_counter_2 (
    .reset(reset), .count(n4_bit_counter_1_cout), .load(load), .\input (in[7:4]), .out(out[7:4]),
    .cout(n4_bit_counter_2_cout), .clock(clock));
  _4_bit_counter u_4_bit_counter_3 (
    .reset(reset), .count(n4_bit_counter_2_cout), .load(load), .\input (in[11:8]), .out(out[11:8]),
    .cout(n4_bit_counter_3_cout), .clock(clock));
  _4_bit_counter u_4_bit_counter_4 (
    .reset(reset), .count(n4_bit_counter_3_cout), .load(load), .\input (in[15:12]), .out(out[15:12]),
    .cout(n4_bit_counter_4_cout), .clock(clock));
  _4_bit_counter u_4_bit_counter_5 (
    .reset(reset), .count(n4_bit_counter_4_cout), .load(load), .\input (in[19:16]), .out(out[19:16]),
    .cout(n4_bit_counter_5_cout), .clock(clock));
  _4_bit_counter u_4_bit_counter_6 (
    .reset(reset), .count(n4_bit_counter_5_cout), .load(load), .\input (in[23:20]), .out(out[23:20]),
    .cout(n4_bit_counter_6_cout), .clock(clock));
  _4_bit_counter u_4_bit_counter_7 (
    .reset(reset), .count(n4_bit_counter_6_cout), .load(load), .\input (in[27:24]), .out(out[27:24]),
    .cout(n4_bit_counter_7_cout), .clock(clock));
  _4_bit_counter u_4_bit_counter_8 (
    .reset(reset), .count(n4_bit_counter_7_cout), .load(load), .\input (in[31:28]), .out(out[31:28]),
    .clock(clock));  // open: cout
  or or_1 (or_1_out, out[0], out[1], out[2], out[3], out[4], out[5], out[6], out[7], out[8], out[9], out[10], out[11], out[12], out[13], out[14], out[15], out[16], out[17], out[18], out[19], out[20], out[21], out[22], out[23], out[24], out[25], out[26], out[27], out[28], out[29], out[30], out[31]);
  not not_1 (MBR_zero, or_1_out);

  // Notes on the sheet:
  //   2207109
endmodule

// IR
module Instruction_reg (
  input  reset,
  input  load,
  input  clock,
  input  [3:0] in,
  output [3:0] out
);

  Load_register load_register_1 (.Input(in), .\output (out), .load(load), .Clock(clock), .reset(reset));

  // Notes on the sheet:
  //   2207109
endmodule

module _1_bit_load_reg (
  input  clock,
  input  reset,
  input  load,
  input  in,
  output out
);

  wire and_1_out, and_2_out, not_1_out, or_1_out;

  not not_1 (not_1_out, load);
  and and_1 (and_1_out, out, not_1_out);
  and and_2 (and_2_out, load, in);
  or or_1 (or_1_out, and_1_out, and_2_out);
  D_Flip_Flop d_ff_1 (.clk(clock), .D(or_1_out), .Q(out), .reset(reset));  // open: Qn, preset, en

  // Notes on the sheet:
  //   2207109
endmodule

module MAR (
  input  clock,
  input  load,
  input  reset,
  input  [4:0] in,
  output [4:0] out
);

  Load_register load_register_1 (.Input(in[3:0]), .\output (out[3:0]), .load(load), .Clock(clock), .reset(reset));
  _1_bit_load_reg u_1_bit_load_reg_1 (.in(in[4]), .load(load), .out(out[4]), .reset(reset), .clock(clock));

  // Notes on the sheet:
  //   2207109
endmodule

module _4_bit_counter (
  input  clock,
  input  reset,
  input  count,
  input  load,
  input  [3:0] \input ,
  output [3:0] out,
  output cout
);

  wire and_1_out, and_2_out, and_3_out, and_4_out, and_5_out, and_6_out, and_7_out, and_8_out, and_9_out,
       and_10_out, and_11_out, and_12_out, not_1_out, not_2_out, not_3_out, not_4_out, not_5_out, or_1_out,
       or_2_out, or_3_out, or_4_out, or_5_out, or_6_out, or_7_out, or_8_out;

  not not_1 (not_1_out, load);
  and and_1 (and_1_out, count, not_1_out);
  and and_2 (and_2_out, load, \input [0]);
  and and_3 (and_3_out, load, not_2_out);
  not not_2 (not_2_out, \input [0]);
  and and_4 (and_4_out, load, \input [1]);
  and and_5 (and_5_out, load, not_3_out);
  not not_3 (not_3_out, \input [1]);
  and and_6 (and_6_out, load, \input [2]);
  and and_7 (and_7_out, load, not_4_out);
  not not_4 (not_4_out, \input [2]);
  and and_8 (and_8_out, load, \input [3]);
  and and_9 (and_9_out, load, not_5_out);
  not not_5 (not_5_out, \input [3]);
  and and_10 (and_10_out, out[0], and_1_out);
  and and_11 (and_11_out, out[0], out[1], and_1_out);
  and and_12 (and_12_out, out[0], out[1], out[2], and_1_out);
  or or_1 (or_1_out, and_1_out, and_2_out);
  or or_2 (or_2_out, and_1_out, and_3_out);
  or or_3 (or_3_out, and_10_out, and_4_out);
  or or_4 (or_4_out, and_10_out, and_5_out);
  or or_5 (or_5_out, and_11_out, and_6_out);
  or or_6 (or_6_out, and_11_out, and_7_out);
  or or_7 (or_7_out, and_12_out, and_8_out);
  or or_8 (or_8_out, and_12_out, and_9_out);
  J_K_Flip_Flop j_k_ff_1 (.J(or_1_out), .clk(clock), .K(or_2_out), .Q(out[0]), .reset(reset));  // open: Qn, preset, en
  J_K_Flip_Flop j_k_ff_2 (.J(or_3_out), .clk(clock), .K(or_4_out), .Q(out[1]), .reset(reset));  // open: Qn, preset, en
  J_K_Flip_Flop j_k_ff_3 (.J(or_5_out), .clk(clock), .K(or_6_out), .Q(out[2]), .reset(reset));  // open: Qn, preset, en
  J_K_Flip_Flop j_k_ff_4 (.J(or_7_out), .clk(clock), .K(or_8_out), .Q(out[3]), .reset(reset));  // open: Qn, preset, en
  and and_13 (cout, out[0], out[1], out[2], out[3]);

  // Notes on the sheet:
  //   2207109
endmodule

// PC
module Program_Counter (
  input  reset,
  input  clock,
  input  load,
  input  count,
  input  [4:0] in,
  output [4:0] \output 
);

  wire and_1_out, and_2_out, and_3_out, and_4_out, n4_bit_counter_1_cout, not_1_out, not_2_out, or_1_out,
       or_2_out;

  and and_1 (and_1_out, count, not_1_out);
  not not_1 (not_1_out, load);
  not not_2 (not_2_out, in[4]);
  and and_2 (and_2_out, load, in[4]);
  and and_3 (and_3_out, load, not_2_out);
  _4_bit_counter u_4_bit_counter_1 (
    .reset(reset), .count(count), .load(load), .\input (in[3:0]), .out(\output [3:0]),
    .cout(n4_bit_counter_1_cout), .clock(clock));
  and and_4 (and_4_out, n4_bit_counter_1_cout, and_1_out);
  or or_1 (or_1_out, and_4_out, and_2_out);
  or or_2 (or_2_out, and_4_out, and_3_out);
  J_K_Flip_Flop j_k_ff_1 (
    .J(or_1_out), .clk(clock), .K(or_2_out), .Q(\output [4]), .reset(reset));  // open: Qn, preset, en

  // Notes on the sheet:
  //   2207109
endmodule

// t
module CPU (
  input  in_1,
  output [31:0] out_2,
  output [4:0] out_3,
  output [3:0] out_4
);

  wire ADD, AND, and_3_out, and_4_out, and_5_out, and_6_out, and_7_out, and_9_out, and_10_out, and_11_out,
       BSB, BUN, Clock, clock_1_out, countMBR, countPC, decoder_1_out13, decoder_1_out14, decoder_1_out15,
       DELAY, E, Ein, F, Fin, Halt, Halt_in, ISZ, Load_Acc, Load_IR, Load_MAR, Load_MBR, Load_op, Load_PC,
       MBR_zero, mod, N, not_1_out, not_2_out, opcode_chk, or_2_out, or_6_out, or_8_out, or_9_out, or_11_out,
       pop, push, Read, STO, SWAP, t0, t1, t2, t3, Write, Z;
  wire [1:0] and_8_out, or_1_out, or_7_out;
  wire [1:1] or_4_out;
  wire [3:0] OpCode;
  wire [4:0] mem_add, n5_bit_mux2_1_out_4, n5_bit_mux4_1_out_6, PC_out;
  wire [4:4] bitselector_2_out;
  wire [22:0] bit_extender_1_out;
  wire [31:0] ACC_in, ACC_out, alu_update_1_out, MBR__in, MBR_out, multiplexer_1_out,
       mux_2_1_32_bit_1_output, mux_4_1_32_bit_1_out_6, mux_4_1_32_bit_2_out_6;

  and and_1 (or_1_out[1], F, pop, t2);
  MUX_4_1_32_bit mux_4_1_32_bit_1 (
    .I1(ACC_in), .I2(MBR_out), .selection(or_1_out), .I4(out_2), .out_6(mux_4_1_32_bit_1_out_6));  // open: I3
  Accumulator accumulator_1 (.in(mux_4_1_32_bit_1_out_6), .load(Load_Acc), .Clock(Clock), .reset(in_1), .out(ACC_out));
  or or_1 (or_1_out[0], Load_op, SWAP, pop);
  Clock clock_1 (.out(clock_1_out));
  not not_1 (not_1_out, Halt);
  and and_2 (Clock, clock_1_out, not_1_out);
  _5_bit_mux2 u_5_bit_mux2_1 (.in_1(mem_add), .in_2(out_3), .S(BSB), .out_4(n5_bit_mux2_1_out_4));
  BitSelector #(.width(32), .group(5)) bitselector_1 (.in(MBR_out), .out(mem_add), .sel(3'b000));
  BitSelector #(.width(32), .group(5)) bitselector_2 (.in(MBR_out), .out({bitselector_2_out[4], OpCode}), .sel(3'b001));
  Program_Counter program_counter_1 (
    .reset(in_1), .clock(Clock), .load(Load_PC), .count(countPC), .in(n5_bit_mux2_1_out_4), .\output (PC_out));
  MUX_2_1_32_Bit mux_2_1_32_bit_1 (
    .I1(MBR_out), .I2(ACC_out), .selection(and_3_out), .\output (mux_2_1_32_bit_1_output));
  and and_3 (and_3_out, F, t3, push);
  RAM #(.addrWidth(5), .dataWidth(32), .bus("separate")) ram_1 (
    .addr(out_3), .din(mux_2_1_32_bit_1_output), .data(out_2), .str(Write), .clk(Clock), .ld(Read));  // open: sel, clr
  assign bit_extender_1_out = {{22{1'b0}}, 1'b0};  // Bit_Extender bit_extender_1
  or or_2 (or_2_out, push, DELAY);
  and and_4 (and_4_out, F, t2, pop);
  or or_3 (or_7_out[1], or_8_out, and_5_out);
  and and_5 (and_5_out, BSB, F);
  or or_4 (or_4_out[1], mod, push, ADD, DELAY);
  control_unit control_unit_1 (
    .F(F), .MBR_zero(MBR_zero), .AND(AND), .write(Write), .ADD(ADD), .opcode_chk(opcode_chk),
    .countPC(countPC), .STO(STO), .Load_MBR(Load_MBR), .BSB(BSB), .Read(Read), .ISZ(ISZ),
    .Load_MAR(Load_MAR), .LOAD_OP(Load_op), .Load_IR(Load_IR), .DELAY(DELAY), .Fin(Fin), .BUN(BUN),
    .Load_PC(Load_PC), .SWAP(SWAP), .Load_Acc(Load_Acc), .countMBR(countMBR), .t0(t0), .t1(t1), .t2(t2),
    .t3(t3), .push(push), .pop(pop), .pre_opcode(OpCode), .mod(mod), .Z(Z), .N(N));
  or or_5 (and_8_out[1], and_4_out, and_6_out);
  and and_6 (and_6_out, t3, or_6_out);
  or or_6 (or_6_out, pop, push);
  MUX_4_1_32_bit mux_4_1_32_bit_2 (
    .I1(out_2), .I2(ACC_out), .selection(or_7_out), .I3({bit_extender_1_out, 4'b0101, PC_out}), .I4(MBR__in),
    .out_6(mux_4_1_32_bit_2_out_6));
  or or_7 (or_7_out[0], or_8_out, and_9_out);
  and and_7 (and_7_out, t2, SWAP);
  Multiplexer #(.width(32), .enable("false")) multiplexer_1 (
    .in0(ACC_out), .in1({32{1'b1}}), .out(multiplexer_1_out), .sel(or_2_out));
  _5_bit_mux4 u_5_bit_mux4_1 (
    .I1(PC_out), .I2(mem_add), .selection(and_8_out), .I3({5{1'b1}}), .out_6(n5_bit_mux4_1_out_6));  // open: I4
  and and_8 (and_8_out[0], F, not_2_out);
  not not_2 (not_2_out, and_4_out);
  or or_8 (or_8_out, and_10_out, and_11_out);
  and and_9 (and_9_out, F, or_9_out);
  or or_9 (or_9_out, and_7_out, STO);
  or or_10 (opcode_chk, AND, ADD, STO, ISZ, BSB, 1'b0, Halt_in, Load_op, DELAY, SWAP, push, pop, mod, decoder_1_out13, decoder_1_out14, decoder_1_out15);
  MAR mar_1 (.in(n5_bit_mux4_1_out_6), .load(Load_MAR), .clock(Clock), .reset(in_1), .out(out_3));
  MBR mbr_1 (
    .in(mux_4_1_32_bit_2_out_6), .load(Load_MBR), .count(countMBR), .clock(Clock), .reset(in_1),
    .out(MBR_out), .MBR_zero(MBR_zero));
  and and_10 (and_10_out, DELAY, F, t2);
  and and_11 (and_11_out, push, F, t1);
  Decoder #(.select(4), .enable("false")) decoder_1 (
    .out0(AND), .out1(ADD), .out2(STO), .out3(ISZ), .out4(BSB), .out5(BUN), .out6(Halt_in), .out7(Load_op),
    .out8(DELAY), .out9(SWAP), .out10(push), .out11(pop), .out12(mod), .out13(decoder_1_out13),
    .out14(decoder_1_out14), .out15(decoder_1_out15), .sel(out_4));
  ALU_update alu_update_1 (
    .control({or_4_out[1], mod}), .A(multiplexer_1_out), .B(MBR_out), .out(alu_update_1_out), .z(Z), .n(N),
    .carry(Ein));  // open: overflow
  // Probe on ACC_in
  Demultiplexer #(.width(32), .enable("false")) demultiplexer_1 (
    .out0(ACC_in), .out1(MBR__in), .in(alu_update_1_out), .sel(or_11_out));
  or or_11 (or_11_out, push, DELAY);
  Instruction_reg instruction_reg_1 (.in(OpCode), .load(Load_IR), .clock(Clock), .reset(in_1), .out(out_4));
  Timer_Decoder timer_decoder_1 (
    .t0(t0), .t1(t1), .t2(t2), .t3(t3), .Reset(in_1), .DELAY(DELAY), .MBR_zero(MBR_zero), .Clock(Clock),
    .mod(mod), .Z(Z), .N(N));  // open: Timer_output
  J_K_Flip_Flop u_F (.J(Fin), .clk(Clock), .K(Fin), .Q(F), .reset(in_1));  // open: Qn, preset, en
  D_Flip_Flop u_E (.clk(Clock), .D(Ein), .Q(E), .reset(in_1));  // open: Qn, preset, en
  D_Flip_Flop S (.clk(Clock), .D(Halt_in), .Q(Halt), .reset(in_1));  // open: Qn, preset, en

  // Other names for the same wires on the sheet: IR_out[3:0] = out_4; MAR_out[4:0] = out_3; pre_opcode[3:0] = OpCode;
  //   RAM_out[31:0] = out_2; Reset = in_1

  // Notes on the sheet:
  //   Accumulator
  //   MBR out splitter
  //   Program Counter
  //   RAM
  //   Control Unit
  //   OpCode Decoder
  //   ALU
  //   Memory Address Register
  //   Memory Buffer Register
  //   2207109
  //   Instruction Register
  //   F,E,S flip flops
  //   Timer Decoder
endmodule

// Timer
module Timer_Decoder (
  input  Reset,
  input  Clock,
  input  DELAY,
  input  MBR_zero,
  input  mod,
  input  Z,
  input  N,
  output t0,
  output t1,
  output [3:0] Timer_output,
  output t2,
  output t3
);

  wire and_1_out, and_2_out, and_3_out, multiplexer_1_out, nor_1_out, not_1_out, or_1_out, or_2_out;
  wire [3:0] multiplexer_2_out;

  nor nor_1 (nor_1_out, Z, N);
  not not_1 (not_1_out, MBR_zero);
  and and_1 (and_1_out, mod, nor_1_out);
  Decoder #(.select(2), .enable("false")) decoder_1 (
    .out0(t0), .out1(t1), .out2(t2), .out3(t3), .sel(Timer_output[1:0]));
  or or_1 (or_1_out, Timer_output[2], Reset);
  and and_2 (and_2_out, DELAY, not_1_out, t3);
  and and_3 (and_3_out, t3, and_1_out);
  _4_bit_counter u_4_bit_counter_1 (
    .reset(or_1_out), .count(1'b1), .load(multiplexer_1_out), .\input (multiplexer_2_out),
    .out(Timer_output), .clock(Clock));  // open: cout
  or or_2 (or_2_out, and_2_out, and_3_out);
  Multiplexer #(.enable("false")) multiplexer_1 (.in0(1'b0), .in1(1'b1), .out(multiplexer_1_out), .sel(or_2_out));
  Multiplexer #(.width(4), .enable("false")) multiplexer_2 (
    .in0(4'b0001), .in1(4'b0010), .out(multiplexer_2_out), .sel(and_1_out));

  // Notes on the sheet:
  //   Timer Decoder
  //   2207109
endmodule

module control_unit (
  input  push,
  input  pop,
  input  [3:0] pre_opcode,
  input  mod,
  input  Z,
  input  N,
  input  MBR_zero,
  input  opcode_chk,
  input  F,
  input  AND,
  input  ADD,
  input  STO,
  input  BSB,
  input  ISZ,
  input  LOAD_OP,
  input  DELAY,
  input  BUN,
  input  SWAP,
  input  t0,
  input  t1,
  input  t2,
  input  t3,
  output write,
  output countPC,
  output Load_MBR,
  output Read,
  output Load_MAR,
  output Load_IR,
  output Fin,
  output Load_PC,
  output Load_Acc,
  output countMBR
);

  wire and_1_out, and_2_out, and_3_out, and_4_out, and_5_out, and_6_out, and_7_out, and_8_out, and_9_out,
       and_10_out, and_11_out, and_12_out, and_13_out, and_14_out, and_15_out, and_16_out, and_17_out,
       and_18_out, and_19_out, and_20_out, and_21_out, and_22_out, and_23_out, and_24_out, and_25_out,
       and_26_out, and_28_out, and_29_out, and_30_out, and_31_out, and_32_out, and_33_out, and_34_out,
       and_35_out, and_36_out, and_37_out, and_38_out, and_39_out, and_40_out, nor_1_out, not_1_out,
       not_2_out, not_3_out, not_4_out, not_5_out, not_6_out, not_7_out, not_8_out, not_9_out, not_10_out,
       not_11_out, not_12_out, not_13_out, not_14_out, not_15_out, not_16_out, not_17_out, not_18_out,
       or_1_out, or_2_out, or_3_out, or_5_out, or_6_out, or_11_out, or_12_out, or_14_out;

  or or_1 (or_1_out, push, pop);
  not not_1 (not_1_out, F);
  not not_2 (not_2_out, F);
  not not_3 (not_3_out, N);
  and and_1 (and_1_out, not_3_out, mod);
  and and_2 (and_2_out, F, t3);
  not not_4 (not_4_out, F);
  not not_5 (not_5_out, or_1_out);
  or or_2 (or_2_out, and_3_out, and_4_out);
  and and_3 (and_3_out, t2, F);
  and and_4 (and_4_out, t3, not_1_out);
  nor nor_1 (nor_1_out, Z, N);
  and and_5 (and_5_out, nor_1_out, mod);
  and and_6 (and_6_out, not_2_out, opcode_chk, t3);
  and and_7 (and_7_out, F, t3);
  not not_6 (not_6_out, DELAY);
  and and_8 (and_8_out, DELAY, MBR_zero);
  and and_9 (and_9_out, BUN, t3, not_7_out);
  not not_7 (not_7_out, F);
  and and_10 (and_10_out, F, BSB, t2);
  or or_3 (or_3_out, AND, ADD, LOAD_OP, and_1_out);
  and and_11 (and_11_out, F, ISZ, t2);
  and and_12 (and_12_out, F, pop, t2);
  and and_13 (and_13_out, and_2_out, STO);
  and and_14 (and_14_out, and_2_out, ISZ);
  and and_15 (and_15_out, not_4_out, t0);
  or or_4 (Load_MAR, and_15_out, and_16_out, and_17_out, and_18_out);
  and and_16 (and_16_out, t0, not_5_out);
  and and_17 (and_17_out, or_1_out, or_2_out);
  and and_18 (and_18_out, F, t1, pop);
  not not_8 (not_8_out, and_5_out);
  or or_5 (or_5_out, and_6_out, and_19_out);
  and and_19 (and_19_out, and_7_out, or_6_out);
  or or_6 (or_6_out, not_6_out, and_8_out);
  or or_7 (Load_PC, and_9_out, and_10_out);
  and and_20 (and_20_out, F, or_3_out, t3);
  and and_21 (and_21_out, F, t2, SWAP);
  and and_22 (and_22_out, and_2_out, DELAY);
  and and_23 (and_23_out, and_2_out, SWAP);
  and and_24 (and_24_out, and_2_out, push);
  and and_25 (and_25_out, and_2_out, pop);
  and and_26 (and_26_out, push, t2, F);
  and and_27 (Fin, not_8_out, or_5_out, not_9_out);
  not not_9 (not_9_out, BUN);
  or or_8 (Load_Acc, and_20_out, and_21_out, and_28_out);
  and and_28 (and_28_out, F, pop, t2);
  or or_9 (countMBR, and_11_out, and_12_out);
  and and_29 (and_29_out, F, BSB, t3);
  not not_10 (not_10_out, F);
  not not_11 (not_11_out, F);
  not not_12 (not_12_out, F);
  or or_10 (write, and_29_out, and_13_out, and_14_out, and_22_out, and_23_out, and_24_out, and_25_out, and_26_out);
  not not_13 (not_13_out, F);
  not not_14 (not_14_out, pre_opcode[0]);
  not not_15 (not_15_out, pre_opcode[2]);
  not not_16 (not_16_out, pre_opcode[2]);
  and and_30 (and_30_out, and_14_out, MBR_zero);
  and and_31 (and_31_out, t1, not_13_out);
  and and_32 (and_32_out, t1, F);
  or or_11 (or_11_out, AND, ADD, STO, BSB, ISZ, LOAD_OP, DELAY, SWAP, push, mod);
  and and_33 (and_33_out, not_10_out, not_14_out, pre_opcode[1], not_15_out, pre_opcode[3], t2);
  and and_34 (and_34_out, not_11_out, pre_opcode[0], pre_opcode[1], not_16_out, pre_opcode[3], t2);
  not not_17 (not_17_out, pre_opcode[1]);
  not not_18 (not_18_out, pre_opcode[3]);
  and and_35 (and_35_out, and_32_out, or_11_out);
  and and_36 (and_36_out, not_12_out, pre_opcode[0], not_17_out, pre_opcode[2], not_18_out, t2);
  and and_37 (and_37_out, F, t2);
  or or_12 (or_12_out, push, pop);
  or or_13 (Load_IR, and_4_out, and_33_out, and_34_out, and_36_out);
  and and_38 (and_38_out, and_37_out, or_14_out);
  or or_14 (or_14_out, BSB, STO, DELAY, SWAP);
  and and_39 (and_39_out, F, t0, or_12_out);
  or or_15 (countPC, and_29_out, and_30_out, and_31_out);
  or or_16 (Load_MBR, and_31_out, and_35_out, and_38_out, and_39_out);
  and and_40 (and_40_out, F, t2, pop);
  or or_17 (Read, Load_MBR, and_40_out);

  // Notes on the sheet:
  //   Logic
  //   Input
  //   Output
  //   2207109
endmodule

// mux2
module MUX_2_1 (
  input  I1,
  input  I2,
  input  selection,
  output \output 
);

  wire and_1_out, and_2_out, not_1_out;

  not not_1 (not_1_out, selection);
  and and_1 (and_1_out, I1, not_1_out);
  and and_2 (and_2_out, I2, selection);
  or or_1 (\output , and_1_out, and_2_out);
endmodule

// mux4
module MUX_4_2 (
  input  I1,
  input  I2,
  input  [1:0] selection,
  input  I3,
  input  I4,
  output out_6
);

  wire mux_2_1_1_output, mux_2_1_2_output;

  MUX_2_1 mux_2_1_1 (.I1(I1), .I2(I2), .selection(selection[0]), .\output (mux_2_1_1_output));
  MUX_2_1 mux_2_1_2 (.I1(I3), .I2(I4), .selection(selection[0]), .\output (mux_2_1_2_output));
  MUX_2_1 mux_2_1_3 (.I1(mux_2_1_1_output), .I2(mux_2_1_2_output), .selection(selection[1]), .\output (out_6));
endmodule

// mux2
module _5_bit_mux2 (
  input  [4:0] in_1,
  input  [4:0] in_2,
  input  S,
  output [4:0] out_4
);

  MUX_2_1 mux_2_1_1 (.I1(in_1[0]), .I2(in_2[0]), .selection(S), .\output (out_4[0]));
  MUX_2_1 mux_2_1_2 (.I1(in_1[1]), .I2(in_2[1]), .selection(S), .\output (out_4[1]));
  MUX_2_1 mux_2_1_3 (.I1(in_1[2]), .I2(in_2[2]), .selection(S), .\output (out_4[2]));
  MUX_2_1 mux_2_1_4 (.I1(in_1[3]), .I2(in_2[3]), .selection(S), .\output (out_4[3]));
  MUX_2_1 mux_2_1_5 (.I1(in_1[4]), .I2(in_2[4]), .selection(S), .\output (out_4[4]));
endmodule

// mux4
module _5_bit_mux4 (
  input  [4:0] I1,
  input  [4:0] I2,
  input  [1:0] selection,
  input  [4:0] I3,
  input  [4:0] I4,
  output [4:0] out_6
);

  wire [4:0] n5_bit_mux2_1_out_4, n5_bit_mux2_2_out_4;

  _5_bit_mux2 u_5_bit_mux2_1 (.in_1(I1), .in_2(I2), .S(selection[0]), .out_4(n5_bit_mux2_1_out_4));
  _5_bit_mux2 u_5_bit_mux2_2 (.in_1(I3), .in_2(I4), .S(selection[0]), .out_4(n5_bit_mux2_2_out_4));
  _5_bit_mux2 u_5_bit_mux2_3 (.in_1(n5_bit_mux2_1_out_4), .in_2(n5_bit_mux2_2_out_4), .S(selection[1]), .out_4(out_6));
endmodule

// mux4
module MUX_2_1_32_Bit (
  input  [31:0] I1,
  input  [31:0] I2,
  input  selection,
  output [31:0] \output 
);

  wire [31:0] and_1_out, and_2_out, not_1_out;

  assign not_1_out = ~{32{selection}};  // NOT_Gate not_1, 32 bits wide
  assign and_1_out = I1 & not_1_out;  // AND_Gate and_1, 32 bits wide
  assign and_2_out = I2 & {32{selection}};  // AND_Gate and_2, 32 bits wide
  assign \output  = and_1_out | and_2_out;  // OR_Gate or_1, 32 bits wide
endmodule

// MUX4
module MUX_4_1_32_bit (
  input  [31:0] I1,
  input  [31:0] I2,
  input  [1:0] selection,
  input  [31:0] I3,
  input  [31:0] I4,
  output [31:0] out_6
);

  wire [31:0] mux_2_1_32_bit_1_output, mux_2_1_32_bit_2_output;

  MUX_2_1_32_Bit mux_2_1_32_bit_1 (.I1(I1), .I2(I2), .selection(selection[0]), .\output (mux_2_1_32_bit_1_output));
  MUX_2_1_32_Bit mux_2_1_32_bit_2 (.I1(I3), .I2(I4), .selection(selection[0]), .\output (mux_2_1_32_bit_2_output));
  MUX_2_1_32_Bit mux_2_1_32_bit_3 (
    .I1(mux_2_1_32_bit_1_output), .I2(mux_2_1_32_bit_2_output), .selection(selection[1]), .\output (out_6));
endmodule
